// Digital circuit 16bite_sumator.dig as structural Verilog
module _16bite_sumator (
  input  A1,
  input  B1,
  input  Cary,
  input  B2,
  input  B3,
  input  B4,
  input  B5,
  input  B6,
  input  B7,
  input  B8,
  input  B9,
  input  B10,
  input  B11,
  input  B12,
  input  B13,
  input  B14,
  input  B15,
  input  B16,
  input  A2,
  input  A3,
  input  A4,
  input  A5,
  input  A6,
  input  A7,
  input  A8,
  input  A9,
  input  A10,
  input  A11,
  input  A12,
  input  A13,
  input  A14,
  input  A15,
  input  A16,
  output Out1,
  output Out2,
  output Out3,
  output Out4,
  output Out5,
  output Out6,
  output Out7,
  output Out8,
  output Out9,
  output Out10,
  output Out11,
  output Out12,
  output Out13,
  output Out14,
  output Out15,
  output Out16,
  output Out_cary
);

  wire sumator_1_cout, sumator_2_cout, sumator_3_cout, sumator_4_cout, sumator_5_cout, sumator_6_cout,
       sumator_7_cout, sumator_8_cout, sumator_9_cout, sumator_10_cout, sumator_11_cout, sumator_12_cout,
       sumator_13_cout, sumator_14_cout, sumator_15_cout;

  Sumator sumator_1 (.Cin(Cary), .A(A1), .B(B1), .Output(Out1), .Cout(sumator_1_cout));
  Sumator sumator_2 (.Cin(sumator_1_cout), .A(A2), .B(B2), .Output(Out2), .Cout(sumator_2_cout));
  Sumator sumator_3 (.Cin(sumator_2_cout), .A(A3), .B(B3), .Output(Out3), .Cout(sumator_3_cout));
  Sumator sumator_4 (.Cin(sumator_3_cout), .A(A4), .B(B4), .Output(Out4), .Cout(sumator_4_cout));
  Sumator sumator_5 (.Cin(sumator_4_cout), .A(A5), .B(B5), .Output(Out5), .Cout(sumator_5_cout));
  Sumator sumator_6 (.Cin(sumator_5_cout), .A(A6), .B(B6), .Output(Out6), .Cout(sumator_6_cout));
  Sumator sumator_7 (.Cin(sumator_6_cout), .A(A7), .B(B7), .Output(Out7), .Cout(sumator_7_cout));
  Sumator sumator_8 (.Cin(sumator_7_cout), .A(A8), .B(B8), .Output(Out8), .Cout(sumator_8_cout));
  Sumator sumator_9 (.Cin(sumator_8_cout), .A(A9), .B(B9), .Output(Out9), .Cout(sumator_9_cout));
  Sumator sumator_10 (.Cin(sumator_9_cout), .A(A10), .B(B10), .Output(Out10), .Cout(sumator_10_cout));
  Sumator sumator_11 (.Cin(sumator_10_cout), .A(A11), .B(B11), .Output(Out11), .Cout(sumator_11_cout));
  Sumator sumator_12 (.Cin(sumator_11_cout), .A(A12), .B(B12), .Output(Out12), .Cout(sumator_12_cout));
  Sumator sumator_13 (.Cin(sumator_12_cout), .A(A13), .B(B13), .Output(Out13), .Cout(sumator_13_cout));
  Sumator sumator_14 (.Cin(sumator_13_cout), .A(A14), .B(B14), .Output(Out14), .Cout(sumator_14_cout));
  Sumator sumator_15 (.Cin(sumator_14_cout), .A(A15), .B(B15), .Output(Out15), .Cout(sumator_15_cout));
  Sumator sumator_16 (.Cin(sumator_15_cout), .A(A16), .B(B16), .Output(Out16), .Cout(Out_cary));
endmodule
