// Digital circuit 1bit_registor.dig as structural Verilog
module _1bit_registor (
  input  Data1,
  input  Data2,
  input  Data3,
  input  Data4,
  input  Data5,
  input  Data6,
  input  Data7,
  input  Data8,
  input  Data9,
  input  Data10,
  input  Data11,
  input  Data12,
  input  Data13,
  input  Data14,
  input  Data15,
  input  Data16,
  input  ComA,
  input  ComB,
  input  Clock,
  output OutA1,
  output OutA2,
  output OutA3,
  output OutA4,
  output OutA5,
  output OutA6,
  output OutA7,
  output OutA8,
  output OutA9,
  output OutA10,
  output OutA11,
  output OutA12,
  output OutA13,
  output OutA14,
  output OutA15,
  output OutA16,
  output OutB1,
  output OutB2,
  output OutB3,
  output OutB4,
  output OutB5,
  output OutB6,
  output OutB7,
  output OutB8,
  output OutB9,
  output OutB10,
  output OutB11,
  output OutB12,
  output OutB13,
  output OutB14,
  output OutB15,
  output OutB16
);

  wire d_triger_1_q, d_triger_2_q, d_triger_5_q, d_triger_8_q, d_triger_11_q, d_triger_14_q, d_triger_17_q,
       d_triger_20_q, d_triger_23_q, d_triger_26_q, d_triger_29_q, d_triger_32_q, d_triger_35_q,
       d_triger_38_q, d_triger_41_q, d_triger_44_q;

  d_triger d_triger_1 (.data(Data1), .clock(Clock), .Q(d_triger_1_q));
  d_triger d_triger_2 (.data(Data2), .clock(Clock), .Q(d_triger_2_q));
  d_triger d_triger_3 (.data(Data2), .clock(Clock), .Q(d_triger_2_q));
  d_triger d_triger_4 (.data(Data2), .clock(Clock), .Q(d_triger_2_q));
  d_triger d_triger_5 (.data(Data3), .clock(Clock), .Q(d_triger_5_q));
  d_triger d_triger_6 (.data(Data3), .clock(Clock), .Q(d_triger_5_q));
  d_triger d_triger_7 (.data(Data3), .clock(Clock), .Q(d_triger_5_q));
  d_triger d_triger_8 (.data(Data4), .clock(Clock), .Q(d_triger_8_q));
  d_triger d_triger_9 (.data(Data4), .clock(Clock), .Q(d_triger_8_q));
  d_triger d_triger_10 (.data(Data4), .clock(Clock), .Q(d_triger_8_q));
  d_triger d_triger_11 (.data(Data5), .clock(Clock), .Q(d_triger_11_q));
  d_triger d_triger_12 (.data(Data5), .clock(Clock), .Q(d_triger_11_q));
  d_triger d_triger_13 (.data(Data5), .clock(Clock), .Q(d_triger_11_q));
  d_triger d_triger_14 (.data(Data6), .clock(Clock), .Q(d_triger_14_q));
  d_triger d_triger_15 (.data(Data6), .clock(Clock), .Q(d_triger_14_q));
  d_triger d_triger_16 (.data(Data6), .clock(Clock), .Q(d_triger_14_q));
  d_triger d_triger_17 (.data(Data7), .clock(Clock), .Q(d_triger_17_q));
  d_triger d_triger_18 (.data(Data7), .clock(Clock), .Q(d_triger_17_q));
  d_triger d_triger_19 (.data(Data7), .clock(Clock), .Q(d_triger_17_q));
  d_triger d_triger_20 (.data(Data8), .clock(Clock), .Q(d_triger_20_q));
  d_triger d_triger_21 (.data(Data8), .clock(Clock), .Q(d_triger_20_q));
  d_triger d_triger_22 (.data(Data8), .clock(Clock), .Q(d_triger_20_q));
  d_triger d_triger_23 (.data(Data9), .clock(Clock), .Q(d_triger_23_q));
  d_triger d_triger_24 (.data(Data9), .clock(Clock), .Q(d_triger_23_q));
  d_triger d_triger_25 (.data(Data9), .clock(Clock), .Q(d_triger_23_q));
  d_triger d_triger_26 (.data(Data10), .clock(Clock), .Q(d_triger_26_q));
  d_triger d_triger_27 (.data(Data10), .clock(Clock), .Q(d_triger_26_q));
  d_triger d_triger_28 (.data(Data10), .clock(Clock), .Q(d_triger_26_q));
  d_triger d_triger_29 (.data(Data11), .clock(Clock), .Q(d_triger_29_q));
  d_triger d_triger_30 (.data(Data11), .clock(Clock), .Q(d_triger_29_q));
  d_triger d_triger_31 (.data(Data11), .clock(Clock), .Q(d_triger_29_q));
  d_triger d_triger_32 (.data(Data12), .clock(Clock), .Q(d_triger_32_q));
  d_triger d_triger_33 (.data(Data12), .clock(Clock), .Q(d_triger_32_q));
  d_triger d_triger_34 (.data(Data12), .clock(Clock), .Q(d_triger_32_q));
  d_triger d_triger_35 (.data(Data13), .clock(Clock), .Q(d_triger_35_q));
  d_triger d_triger_36 (.data(Data13), .clock(Clock), .Q(d_triger_35_q));
  d_triger d_triger_37 (.data(Data13), .clock(Clock), .Q(d_triger_35_q));
  d_triger d_triger_38 (.data(Data14), .clock(Clock), .Q(d_triger_38_q));
  d_triger d_triger_39 (.data(Data14), .clock(Clock), .Q(d_triger_38_q));
  d_triger d_triger_40 (.data(Data14), .clock(Clock), .Q(d_triger_38_q));
  d_triger d_triger_41 (.data(Data15), .clock(Clock), .Q(d_triger_41_q));
  d_triger d_triger_42 (.data(Data15), .clock(Clock), .Q(d_triger_41_q));
  d_triger d_triger_43 (.data(Data15), .clock(Clock), .Q(d_triger_41_q));
  d_triger d_triger_44 (.data(Data16), .clock(Clock), .Q(d_triger_44_q));
  d_triger d_triger_45 (.data(Data16), .clock(Clock), .Q(d_triger_44_q));
  d_triger d_triger_46 (.data(Data16), .clock(Clock), .Q(d_triger_44_q));
  Tri_state_Buffer tri_state_buffer_1 (
    .ComA(ComA), .DataZbuffer(d_triger_1_q), .ComB(ComB), .DataA(OutB16), .DataB(OutA16));
  Tri_state_Buffer tri_state_buffer_2 (
    .ComA(ComA), .DataZbuffer(d_triger_2_q), .ComB(ComB), .DataA(OutB15), .DataB(OutA15));
  Tri_state_Buffer tri_state_buffer_3 (
    .ComA(ComA), .DataZbuffer(d_triger_5_q), .ComB(ComB), .DataA(OutB14), .DataB(OutA14));
  Tri_state_Buffer tri_state_buffer_4 (
    .ComA(ComA), .DataZbuffer(d_triger_8_q), .ComB(ComB), .DataA(OutB13), .DataB(OutA13));
  Tri_state_Buffer tri_state_buffer_5 (
    .ComA(ComA), .DataZbuffer(d_triger_11_q), .ComB(ComB), .DataA(OutB12), .DataB(OutA12));
  Tri_state_Buffer tri_state_buffer_6 (
    .ComA(ComA), .DataZbuffer(d_triger_14_q), .ComB(ComB), .DataA(OutB11), .DataB(OutA11));
  Tri_state_Buffer tri_state_buffer_7 (
    .ComA(ComA), .DataZbuffer(d_triger_17_q), .ComB(ComB), .DataA(OutB10), .DataB(OutA10));
  Tri_state_Buffer tri_state_buffer_8 (
    .ComA(ComA), .DataZbuffer(d_triger_20_q), .ComB(ComB), .DataA(OutB9), .DataB(OutA9));
  Tri_state_Buffer tri_state_buffer_9 (
    .ComA(ComA), .DataZbuffer(d_triger_23_q), .ComB(ComB), .DataA(OutB8), .DataB(OutA8));
  Tri_state_Buffer tri_state_buffer_10 (
    .ComA(ComA), .DataZbuffer(d_triger_26_q), .ComB(ComB), .DataA(OutB7), .DataB(OutA7));
  Tri_state_Buffer tri_state_buffer_11 (
    .ComA(ComA), .DataZbuffer(d_triger_29_q), .ComB(ComB), .DataA(OutB6), .DataB(OutA6));
  Tri_state_Buffer tri_state_buffer_12 (
    .ComA(ComA), .DataZbuffer(d_triger_32_q), .ComB(ComB), .DataA(OutB5), .DataB(OutA5));
  Tri_state_Buffer tri_state_buffer_13 (
    .ComA(ComA), .DataZbuffer(d_triger_35_q), .ComB(ComB), .DataA(OutB4), .DataB(OutA4));
  Tri_state_Buffer tri_state_buffer_14 (
    .ComA(ComA), .DataZbuffer(d_triger_38_q), .ComB(ComB), .DataA(OutB3), .DataB(OutA3));
  Tri_state_Buffer tri_state_buffer_15 (
    .ComA(ComA), .DataZbuffer(d_triger_41_q), .ComB(ComB), .DataA(OutB2), .DataB(OutA2));
  Tri_state_Buffer tri_state_buffer_16 (
    .ComA(ComA), .DataZbuffer(d_triger_44_q), .ComB(ComB), .DataA(OutB1), .DataB(OutA1));
endmodule
