// Digital circuit d_triger.dig as structural Verilog
module d_triger (
  input  Data,
  input  Clock,
  output out
);

  wire nand_1_out, nand_2_out, nand_4_out;

  nand nand_1 (nand_1_out, Data, Clock);
  nand nand_2 (nand_2_out, nand_1_out, Clock);
  nand nand_3 (out, nand_1_out, nand_4_out);
  nand nand_4 (nand_4_out, out, nand_2_out);
endmodule
